# Fritzing sketch design (saved by Fritzing 0.9.3b)
breadboards: 1

parts:
  LED1 = LED - 5mm [color="Green (570nm)" package="5 mm [THT]"]
  MCU1 = Raspberry Pi Zero
  R1 = Resistor [tolerance=±5% resistance=220 package=THT]
  LCD1 = LCD screen
  S1 = Pushbutton [package="[THT]"]
  S2 = Pushbutton [package="[THT]"]
  S3 = Pushbutton [package="[THT]"]
  R2 = Trimmer Potentiometer [maximum_resistance=10kΩ package=THT]

nets:
  N1: LED1.cathode, MCU1.pin_40
  N2: LED1.anode, R1.Pin_0
  N3: MCU1.pin_2, MCU1.pin_4, LCD1.VDD, LCD1.LED+, R2.leg2
  N4: MCU1.pin_6, MCU1.pin_9, MCU1.pin_20, MCU1.pin_39, R1.Pin_1, LCD1.VSS, LCD1.R/W, LCD1.LED-, S1.Pin_4, S2.Pin_3, S2.Pin_4, S3.Pin_1, S3.Pin_2, S3.Pin_3, S3.Pin_4, R2.leg1
  N5: MCU1.pin_11, LCD1.DB5
  N6: MCU1.pin_12, LCD1.DB6
  N7: MCU1.pin_15, LCD1.DB7
  N8: MCU1.pin_16, LCD1.DB4
  N9: MCU1.pin_18, LCD1.E
  N10: MCU1.pin_22, LCD1.RS
  N11: MCU1.pin_35, S1.Pin_2
  N12: MCU1.pin_37, S2.Pin_1, S2.Pin_2
  N13: LCD1.V0, R2.wiper
